# Fritzing sketch drawing (saved by Fritzing 0.9.3b)

parts:
  U2 = Vishay ILQ [package=THT]
  R1 = Resistor [tolerance=±5% resistance=22k package=THT]
  R2 = Resistor [tolerance=±5% resistance=22k package=THT]
  R3 = Resistor [tolerance=±5% resistance=22k package=THT]
  R4 = Resistor [tolerance=±5% resistance=22k package=THT]
  R5 = Resistor [tolerance=±5% resistance=22k package=THT]
  R6 = Resistor [tolerance=±5% resistance=820 package=THT]
  R7 = Resistor [tolerance=±5% resistance=820 package=THT]
  R8 = Resistor [tolerance=±5% resistance=820 package=THT]
  R9 = Resistor [tolerance=±5% resistance=820 package=THT]
  J3 = Camdenboss CTB0158-5 [part_number=CTB0158-5 package=THT]
  J2 = Camdenboss CTB0158-5 [part_number=CTB0158-5 package=THT]
  Part1 = Arduino Nano (Rev3.0) (ICSP)
  J1 = Camdenboss CTB0158-6 [part_number=CTB0158-6 package=THT]
  J4 = Camdenboss CTB0158-2 [part_number=CTB0158-2 package=THT]

nets:
  N1: U2.Pin_1, R6.Pin_1
  GND: U2.Pin_2, U2.Pin_3, U2.Pin_6, U2.Pin_7, R2.Pin_1, R3.Pin_1, R4.Pin_1, R5.Pin_1, J3.pin1, J2.pin5, Part1.GND, J1.pin6, J4.pin1
  N2: U2.Pin_4, R7.Pin_1
  N3: U2.Pin_5, R8.Pin_1
  N4: U2.Pin_8, R9.Pin_1
  N5: U2.Pin_9, R2.Pin_0
  Frequency: U2.Pin_10, R1.Pin_0, J1.pin1
  12V: U2.Pin_11, U2.Pin_14, U2.Pin_15, R1.Pin_1, J1.pin5
  FWD: U2.Pin_12, R3.Pin_0, J1.pin4
  REV: U2.Pin_13, R4.Pin_0, J1.pin3
  EXTFLT: U2.Pin_16, R5.Pin_0, J1.pin2
  N6: R6.Pin_0, Part1.D10
  N7: R7.Pin_0, Part1.D7
  N8: R8.Pin_0, Part1.D6
  N9: R9.Pin_0, Part1.D3
  OpenedRes: J3.pin2, Part1.A7
  ClosedRes: J3.pin3, Part1.A6
  Opened: J3.pin4, Part1.A5
  Closed: J3.pin5, Part1.A4
  N10: J2.pin1, Part1.A3
  Stop: J2.pin2, Part1.A2
  Close: J2.pin3, Part1.A1
  Open: J2.pin4, Part1.A0
  N11: Part1.VIN, J4.pin2
  3.3V: Part1.3V3

notes:
  GND
  Open
  Close
  Stop
  OpenedRes
  ClosedRes
  Opened
  Closed
  Reserve
  +5..12V

custom parts:
  Vishay ILQ: Optocoupler with four channels on one chip
